# Fritzing sketch schematics_mini_sec_sys (saved by Fritzing 0.9.3b)
breadboards: 2

parts:
  Part1 = Arduino Nano (Rev3.0)
  J1 = Basic Servo
  LED1 = LED - 5mm [color="Blue (505nm)" package="5 mm [THT]"]
  LED2 = LED - 5mm [color="Blue (505nm)" package="5 mm [THT]"]
  LED3 = LED - 5mm [color="Red (633nm)" package="5 mm [THT]"]
  R1 = Resistor [tolerance=±5% resistance=220 package=THT]
  R2 = Resistor [tolerance=±5% resistance=220 package=THT]
  R3 = Resistor [tolerance=±5% resistance=220 package=THT]
  Part2 = SRF05 Ultrasonic Rangefinder
  J2 = Basic Servo
  Part3 = SPI OLED Monochrome 128x64 0.96 inch

nets:
  N1: Part1.RESET, Part3.RES
  GND: Part1.GND, Part2.GND
  N2: Part1.D2, R3.Pin_0
  N3: Part1.D3, R2.Pin_0
  N4: Part1.D4, R1.Pin_0
  N5: Part1.D5, J1.pulse
  N6: Part1.D6, J2.pulse
  N7: Part1.D9, Part3.DC
  N8: Part1.D10, Part3.CS
  N9: Part1.D11/MOSI, Part3.SDA
  VCC: Part1.5V, J1.vcc, Part2.VCC, J2.vcc, Part3.VDD
  N10: Part1.A2, Part2.Echo
  N11: Part1.A1, Part2.Trig
  N12: Part1.D13/SCK, Part3.SCK
  GND_2: J1.gnd, LED1.cathode, LED2.cathode, LED3.cathode, J2.gnd, Part3.GND
  N13: LED1.anode, R2.Pin_1
  N14: LED2.anode, R1.Pin_1
  N15: LED3.anode, R3.Pin_1

custom parts:
  SPI OLED Monochrome 128x64 0.96 inch: Unknown 128x64 0.96 inch 128x64 SPI Monochrome OLED display
